# Fritzing sketch Sim800l (saved by Fritzing 0.9.3b)
breadboards: 1

parts:
  GSM_SIM_GPSR_SMS_SIM900_SIM1 = SIM800L [package=THT]
  S1 = Pushbutton [package="[THT]"]
  S2 = Pushbutton [package="[THT]"]
  S3 = Pushbutton [package="[THT]"]
  Pro_Micro2 = Pro Micro  # not connected
  Q1 = NPN-Transistor [package="TO92 [THT]"]
  Nokia_5110_LCD_Module3 = Nokia5110LCDModule
  R1 = Resistor [tolerance=±5% resistance=220 package="1206 [SMD]"]

nets:
  N1: GSM_SIM_GPSR_SMS_SIM900_SIM1.5V, Nokia_5110_LCD_Module3.6_DN_(MOSI)
  N2: GSM_SIM_GPSR_SMS_SIM900_SIM1.GND#1, Q1.E
  N3: S1.Pin_1, S1.Pin_2
  N4: S1.Pin_3, S1.Pin_4, S2.Pin_3, S2.Pin_4, S3.Pin_3, S3.Pin_4, Q1.C, Nokia_5110_LCD_Module3.LED
  N5: S2.Pin_1, S2.Pin_2
  N6: S3.Pin_1, S3.Pin_2
  N7: Q1.B, R1.Pin_0

custom parts:
  Pro Micro: The SparkFun Pro Micro is a complete USB-based microcontoller development system, in a very small footprint, capable of implementing many types of projects. All programming can be done via the USB port.
  : Nokia 5110 LCD with 8 pin. It's a 45mm*45mm module part. Description: The Nokia 5110 is a basic graphic LCD screen for lots of applications. It was originally intended for as a cell phone screen. This one is mounted on an easy to solder PCB. It uses the PCD8544 controller. The PCD8544 is a low power CMOS LCD controller/driver, designed to drive a graphic display of 48 rows and 84 columns. All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
